# Fritzing sketch wiring-withANano (saved by Fritzing 1.0.6)
breadboards: 6

parts:
  A1 = Waveshare ESP32-Pico  # not connected
  M1 = RPlidar A2M8 [package=THT]  # not connected
  DC_Mot_Enc1 = DC Motor with two-phase hall-encoder [part_number=VT-E-G25A-06-177E]  # not connected
  Part1 = Arduino Nano (Rev3.0)
  DC_Mot_Enc2 = DC Motor with two-phase hall-encoder [part_number=VT-E-G25A-06-177E]  # not connected
  DC_Mot_Enc3 = DC Motor with two-phase hall-encoder [part_number=VT-E-G25A-06-177E]  # not connected
  DC_Mot_Enc4 = DC Motor with two-phase hall-encoder [part_number=VT-E-G25A-06-177E]  # not connected
  HC-SR04_Sensor_1 = HC-SR04 Ultrasonic Distance Sensor
  U1 = LIPO-1000mAh [package=lipo-1000]
  M2 = RioRand LM2596
  X1 = USB Connectors [package=usb-microb]  # not connected
  M3 = fc-51 [package=THT]
  M4 = fc-51 [package=THT]
  A3 = Sparkfun sen18642  # not connected
  Part3 = InvenSense MPU6050
  A4 = Hi-link HLK-LD2410C  # not connected
  A5 = Jetson Nano  # not connected
  U2 = LIPO-2000mAh [package=lipo-2000]  # not connected
  Part6 = I2C level shifter bidirectional
  X2 = USB Connectors [package=usb-microb]  # not connected
  M6 = fc-51 [package=THT]
  M7 = fc-51 [package=THT]
  A6 = Sparkfun sen18642
  Part7 = InvenSense MPU6050
  A7 = Hi-link HLK-LD2410C
  U4 = LIPO-2000mAh [package=lipo-2000]
  Part8 = I2C level shifter bidirectional
  HC-SR04_Sensor_2 = HC-SR04 Ultrasonic Distance Sensor
  M8 = RPlidar A2M8 [package=THT]  # not connected
  DC_Mot_Enc5 = DC Motor with two-phase hall-encoder [part_number=VT-E-G25A-06-177E]
  DC_Mot_Enc6 = DC Motor with two-phase hall-encoder [part_number=VT-E-G25A-06-177E]
  DC_Mot_Enc7 = DC Motor with two-phase hall-encoder [part_number=VT-E-G25A-06-177E]
  DC_Mot_Enc8 = DC Motor with two-phase hall-encoder [part_number=VT-E-G25A-06-177E]
  Part9 = Arduino Nano (Rev3.0)
  Mod1 = Raspberry Pi Pico W  # not connected
  J1 = STARBOARD_GND [package=starboard_ground_small2]
  J2 = STARBOARD_GND [package=starboard_ground_small2]  # not connected
  J3 = STARBOARD_GND [package=starboard_ground_small2]
  Mod2 = Raspberry Pi Pico W
  JP5 = Header 5x2 [package=2x5-ra]  # not connected
  JP6 = Header 5x2 [package=2x5-ra]
  JP7 = Header 5x2 [package=2x5-ra]
  JP8 = Header 5x2 [package=2x5-ra]  # not connected
  J4 = STARBOARD_GND [package=starboard_ground_small2]
  J5 = STARBOARD_GND [package=starboard_ground_small2]
  U5 = LIPO-1000mAh [package=lipo-1000]
  M9 = RioRand LM2596
  M10 = fc-51 [package=THT]
  M11 = fc-51 [package=THT]
  A8 = Sparkfun sen18642
  Part10 = InvenSense MPU6050
  A9 = Hi-link HLK-LD2410C
  U6 = LIPO-2000mAh [package=lipo-2000]  # not connected
  Part11 = I2C level shifter bidirectional
  HC-SR04_Sensor_3 = HC-SR04 Ultrasonic Distance Sensor
  M12 = RPlidar A2M8 [package=THT]  # not connected
  DC_Mot_Enc9 = DC Motor with two-phase hall-encoder [part_number=VT-E-G25A-06-177E]
  DC_Mot_Enc10 = DC Motor with two-phase hall-encoder [part_number=VT-E-G25A-06-177E]
  DC_Mot_Enc11 = DC Motor with two-phase hall-encoder [part_number=VT-E-G25A-06-177E]
  DC_Mot_Enc12 = DC Motor with two-phase hall-encoder [part_number=VT-E-G25A-06-177E]
  J8 = Camdenboss CTB0158-4 [part_number=CTB0158-4 package=THT]
  J16 = STARBOARD_GND [package=starboard_ground_small2]
  J6 = STARBOARD_GND [package=starboard_ground_small2]
  J17 = Camdenboss CTB0158-4 [part_number=CTB0158-4 package=THT]
  Mod3 = Raspberry Pi Pico W
  JP12 = Header 5x2 [package=2x5-ra]  # not connected
  J18 = STARBOARD_GND [package=starboard_ground_small2]
  J19 = STARBOARD_GND [package=starboard_ground_small2]
  J20 = STARBOARD_GND [package=starboard_ground_small2]
  J21 = STARBOARD_GND [package=starboard_ground_small2]
  U7 = LIPO-1000mAh [package=lipo-1000]
  M13 = RioRand LM2596
  M14 = fc-51 [package=THT]
  M15 = fc-51 [package=THT]
  A10 = Sparkfun sen18642
  Part12 = InvenSense MPU6050
  A11 = Hi-link HLK-LD2410C
  U8 = LIPO-2000mAh [package=lipo-2000]  # not connected
  Part13 = I2C level shifter bidirectional
  HC-SR04_Sensor_4 = HC-SR04 Ultrasonic Distance Sensor
  M16 = RPlidar A2M8 [package=THT]  # not connected
  DC_Mot_Enc13 = DC Motor with two-phase hall-encoder [part_number=VT-E-G25A-06-177E]
  DC_Mot_Enc14 = DC Motor with two-phase hall-encoder [part_number=VT-E-G25A-06-177E]
  DC_Mot_Enc15 = DC Motor with two-phase hall-encoder [part_number=VT-E-G25A-06-177E]
  DC_Mot_Enc16 = DC Motor with two-phase hall-encoder [part_number=VT-E-G25A-06-177E]
  Part14 = Arduino Nano (Rev3.0)  # not connected
  JP13 = Header 5x2 [package=2x5-ra]
  JP17 = Header 5x2 [package=2x5-ra]
  JP18 = Header 5x2 [package=2x5-ra]  # not connected
  JP19 = Header 5x2 [package=2x5-ra]

nets:
  N1: Part1.D1/TX, Part6.HV2
  N2: Part1.D0/RX, Part6.HV1
  GND: Part1.GND, HC-SR04_Sensor_1.GND, M3.pin2, Part3.GND, Part6.GND
  VCC: Part1.5V, HC-SR04_Sensor_1.VCC, M3.pin3, Part3.VCC, Part6.HV
  N3: Part1.A5, M4.pin1
  N4: Part1.3V3, Part6.LV
  N5: U1.+, M2.Pin_1
  N6: U1.-, M2.Pin_2
  N7: M6.pin1, Part9.D2
  GND_2: M6.pin2, M7.pin2, Part7.GND, A7.Pin_4, Part8.GND, Part9.GND
  N8: M6.pin3, M7.pin3, A7.Pin_5, Part8.HV, Part9.5V
  N9: M7.pin1, Part9.A3
  N10: A6.Pin_6, Part7.VCC, Part8.LV, JP17.1
  N11: A6.Pin_7, Part7.SDA, Part8.LV1, JP19.1
  N12: A6.Pin_8, Part7.SCL, Part8.LV2, JP19.3
  N13: A7.Pin_1, JP17.8
  N14: A7.Pin_2, JP17.10
  N15: U4.-, DC_Mot_Enc5.pin2, DC_Mot_Enc8.pin2, J3.MOUNT
  N16: Part8.HV1, Part9.A4
  N17: Part8.HV2, Part9.A5
  N18: HC-SR04_Sensor_2.TRIG, Part9.A7
  N19: HC-SR04_Sensor_2.ECHO, Part9.A6
  N20: DC_Mot_Enc5.pin3, JP13.1
  N21: DC_Mot_Enc5.pin4, JP13.3
  N22: DC_Mot_Enc6.pin2, DC_Mot_Enc7.pin2, J1.MOUNT
  N23: DC_Mot_Enc6.pin3, JP13.10
  N24: DC_Mot_Enc6.pin4, JP13.8
  N25: DC_Mot_Enc7.pin3, JP13.4
  N26: DC_Mot_Enc7.pin4, JP13.2
  N27: DC_Mot_Enc8.pin3, JP13.7
  N28: DC_Mot_Enc8.pin4, JP13.9
  N29: Mod2.pin_1, A9.Pin_2
  N30: Mod2.pin_2, A9.Pin_1
  N31: Mod2.pin_13, Mod2.pin_18, Mod2.pin_23, DC_Mot_Enc9.pin3, DC_Mot_Enc12.pin3
  N32: Mod2.pin_15, DC_Mot_Enc12.pin4
  N33: Mod2.pin_20, DC_Mot_Enc9.pin4
  N34: Mod2.pin_21, A8.Pin_7, A8.Pin_13, Part10.SDA
  N35: Mod2.pin_22, A8.Pin_8, A8.Pin_14, Part10.SCL
  N36: Mod2.pin_24, DC_Mot_Enc10.pin4
  N37: Mod2.pin_25, DC_Mot_Enc10.pin3
  N38: Mod2.pin_26, DC_Mot_Enc11.pin3
  N39: Mod2.pin_27, DC_Mot_Enc11.pin4
  N40: Mod2.pin_36, A8.Pin_2, A8.Pin_6, Part10.VCC, Part11.LV
  N41: JP6.7, Part11.LV4
  N42: JP7.1, Part11.LV3
  N43: JP7.3, Part11.LV2
  N44: JP7.7, Part11.LV1
  N45: J4.MOUNT, DC_Mot_Enc9.pin2, DC_Mot_Enc10.pin2, DC_Mot_Enc11.pin2, DC_Mot_Enc12.pin2
  N46: J5.MOUNT, A9.Pin_4
  N47: U5.+, M9.Pin_1
  N48: U5.-, M9.Pin_2, M9.Pin_4, M10.pin2, Part11.GND
  N49: M9.Pin_3, M10.pin3, M11.pin3, A9.Pin_5
  N50: M10.pin1, Part11.HV4
  N51: M11.pin1, Part11.HV1
  N52: M11.pin2, HC-SR04_Sensor_3.GND, J6.MOUNT
  N53: A8.Pin_5, J16.MOUNT
  N54: Part11.HV2, HC-SR04_Sensor_3.TRIG
  N55: Part11.HV, HC-SR04_Sensor_3.VCC
  N56: Part11.HV3, HC-SR04_Sensor_3.ECHO
  N57: DC_Mot_Enc9.pin5, J8.pin4
  N58: DC_Mot_Enc10.pin5, J8.pin2
  N59: DC_Mot_Enc11.pin5, J8.pin1
  N60: DC_Mot_Enc12.pin5, J8.pin3
  N61: J17.pin1, DC_Mot_Enc15.pin5
  N62: J17.pin2, DC_Mot_Enc14.pin5
  N63: J17.pin3, DC_Mot_Enc16.pin5
  N64: J17.pin4, DC_Mot_Enc13.pin5
  N65: Mod3.pin_1, A11.Pin_2
  N66: Mod3.pin_2, A11.Pin_1
  N67: Mod3.pin_13, Mod3.pin_18, Mod3.pin_33, Part13.LV2, DC_Mot_Enc13.pin3, DC_Mot_Enc16.pin3
  N68: Mod3.pin_15, DC_Mot_Enc16.pin4
  N69: Mod3.pin_20, DC_Mot_Enc13.pin4
  N70: Mod3.pin_21, A10.Pin_7, A10.Pin_13, Part12.SDA
  N71: Mod3.pin_22, A10.Pin_8, A10.Pin_14, Part12.SCL
  N72: Mod3.pin_24, DC_Mot_Enc14.pin4
  N73: Mod3.pin_25, DC_Mot_Enc14.pin3
  N74: Mod3.pin_26, DC_Mot_Enc15.pin3
  N75: Mod3.pin_27, DC_Mot_Enc15.pin4
  N76: Mod3.pin_30, Part13.LV4
  N77: Mod3.pin_32, Part13.LV3
  N78: Mod3.pin_34, Part13.LV1
  N79: Mod3.pin_36, A10.Pin_2, A10.Pin_6, Part12.VCC, Part13.LV
  N80: J18.MOUNT, DC_Mot_Enc13.pin2, DC_Mot_Enc14.pin2, DC_Mot_Enc15.pin2, DC_Mot_Enc16.pin2
  N81: J19.MOUNT, A10.Pin_5
  N82: J20.MOUNT, A11.Pin_4
  N83: J21.MOUNT, M15.pin2
  N84: U7.+, M13.Pin_1
  N85: U7.-, M13.Pin_2, M13.Pin_4, M14.pin2, Part13.GND
  N86: M13.Pin_3, M14.pin3, M15.pin3, A11.Pin_5
  N87: M14.pin1, Part13.HV4
  N88: M15.pin1, Part13.HV1
  N89: Part13.HV2, HC-SR04_Sensor_4.TRIG
  N90: Part13.HV, HC-SR04_Sensor_4.VCC
  N91: Part13.HV3, HC-SR04_Sensor_4.ECHO

notes:
  REd=5V/6V power,
  Pink = Signal,
  Black = ground, Orange = 3.3V power
  green/yellow = I2C-ish signal pairs
  SR04 is 5V. Fish sensor is 5V
  motors - encoder can be 3.3-5V. Output will be according to input
  Vl53L5CX is 3.3V power and
  https://learn.sparkfun.com/tutorials/qwiic-tof-imager---vl53l5cx-hookup-guide
  LD2450 power is 5V,200mA. It's Serial port (UART?) TxRx is 3.3V, default baud 256k
  MPU6050 is 3.3 or 5V as per power supply
  ESP32-Pico pins GP39 and GND are interchanged in this model. But onreal piece they are as per datasheet
  Nano V3 is 5V device . Power will be from micro- USB at 5V from the Jetson
  Vl53L5CX is 3.3V power and
  https://learn.sparkfun.com/tutorials/qwiic-tof-imager---vl53l5cx-hookup-guide
  LD2450 power is 5V,200mA. It's Serial port (UART) TxRx is 3.3V, default baud 256k
  motors - encoder can be 3.3-5V. Output will be according to input
  Red = motor+
  White = Motor-
  Yellow - signal feedback,
  Green = signal feedback
  Blue = encoder supply +
  Black = encoder supply -
  Nano V3 is 5V device . Power will be from micro- USB at 5V from the Jetson
  SDA A4(23), SCL A5(24)
  motors - encoder supply can be 3.3-5V. Output will be according to input
  Red = motor+
  White = Motor-
  Yellow - signal feedback,
  Green = signal feedback
  Blue = encoder supply +
  Black = encoder supply -
  Here, the Arduino Nano seems a wasted component causing excess wiring. SO pausing this and drawing teh one on right
  1. LD06 LiDAR Connection (UART)
  The LD06 communicates via serial (UART). It typically requires 5V power but uses 3.3V logic for data, which matches the Jetson's logic level perfectly.
  Protocol: UART (8N1, 230400 baud)
  Jetson Device Path: /dev/ttyTHS1 (Primary UART)
  Signal
  LD06 Wire Color (Typ.)
  Jetson Orin Nano Pin
  Pin Function
  5V
  Red
  Pin 4
  5V Power
  GND
  Black
  Pin 6
  Ground
  TX
  Yellow (or Green)
  Pin 10
  UART1_RX (Receive)
  PWM
  Blue (or White)
  Not Connected
  Motor Control*
  r note here]
  2. I2C Device Connection
  The Jetson Orin Nano has two main I2C buses on the header. Bus 7 is the standard recommended bus for external sensors.
  Jetson Device Path: /dev/i2c-7 (Bus 7) or sometimes /dev/i2c-1 (Bus 1) depending on OS version, but physically these are the pins:
  Signal
  I2C Device Pin
  Jetson Orin Nano Pin
  Pin Function
  SDA
  SDA
  Pin 3
  I2C_2_SDA (Bus 7)
  SCL
  SCL
  Pin 5
  I2C_2_SCL (Bus 7)
  VCC
  VCC
  Pin 1 (3.3V) or Pin 2 (5V)
  Power (Check your device specs)
  GND
  GND
  Pin 9
  Ground
  3. ILI9341 Display Connection (SPI)
  The ILI9341 driver requires a 4-wire SPI connection plus GPIOs for Reset (RST) and Data/Command (DC).
  Protocol: SPI (Mode 0)
  Jetson Device Path: /dev/spidev0.0
  Important: You must enable SPI using the jetson-io tool (see instructions below).
  Signal
  ILI9341 Pin
  Jetson Orin Nano Pin
  Pin Function
  VCC
  VCC
  Pin 2
  5V Power (Most modules have 3.3V regulator)
  GND
  GND
  Pin 14
  Ground
  CS
  CS
  Pin 24
  SPI0_CS0 (Chip Select)
  RESET
  RST
  Pin 22
  GPIO (can use other free GPIO)
  DC
  DC/RS
  Pin 18
  GPIO (can use other free GPIO)
  MOSI
  MOSI/SDA
  Pin 19
  SPI0_MOSI (Master Out)
  SCK
  SCK/CL
  Pin 23
  SPI0_SCK (Clock)
  LED
  LED/BLK
  Pin 1
  3.3V (Always On) or use GPIO for dimming
  MISO
  MISO
  Pin 21
  SPI0_MISO (Master In)
  Critical Step: Enabling the Pins
  By default, the SPI pins on the Jetson Orin Nano might be disabled or set to GPIO mode. To ensure they work:
  Open a terminal on the Jetson.
  Run the configuration tool: sudo /opt/nvidia/jetson-io/jetson-io.py
  Select Configure Jetson 40pin Header.
  Select Configure header pins manually.
  Ensure SPI1 (pins 19, 21, 23, 24, 26) is checked/enabled.
  Save and Reboot the system.
  UART to Jetson
  UART Pico to LD2450

custom parts:
  RPlidar A2M8: .The RPLIDAR A2 is the next generation low cost 360 degree 2D laser scanner (LIDAR) solution developed by SLAMTEC. It can take up to 4000 samples of laser ranging per second with high rotation speed. And equipped with SLAMTEC patented OPTMAG technology, it breakouts the life limitation of traditional LIDAR system so as to work stably for a long time.
  Sparkfun sen18642: The SparkFun Qwiic ToF Imager is built around VL53L5CX from ST Electronics; a state of the art, Time-of-Flight (ToF), multizone ranging sensor.
  Hi-link HLK-LD2410C: LD2410C is a high-sensitivity 24GHz human presence status sensing module. bb reversed for on perfboard in breadboard.
  Raspberry Pi Pico W: Raspberry Pi Pico W. Based around the RP2040 microcontroller the Pico W is a low cost microcontroller device bringing Raspberry Pi quality, cost, and easy of use to the microcontroller space. The areas marked KEEPOUT in pcb silkscreen should not have traces running through them to avoid shorts on a soldered in module!
