# Fritzing sketch wiring-withEsp32 (saved by Fritzing 0.9.6b)
breadboards: 2

parts:
  A1 = Waveshare ESP32-Pico  # not connected
  M1 = RPlidar A2M8 [package=THT]  # not connected
  DC_Mot_Enc1 = DC Motor with two-phase hall-encoder [part_number=VT-E-G25A-06-177E]  # not connected
  Part1 = Arduino Nano (Rev3.0)  # not connected
  DC_Mot_Enc2 = DC Motor with two-phase hall-encoder [part_number=VT-E-G25A-06-177E]  # not connected
  DC_Mot_Enc3 = DC Motor with two-phase hall-encoder [part_number=VT-E-G25A-06-177E]  # not connected
  DC_Mot_Enc4 = DC Motor with two-phase hall-encoder [part_number=VT-E-G25A-06-177E]  # not connected
  HC-SR04_Sensor_1 = HC-SR04 Ultrasonic Distance Sensor
  U1 = LIPO-1000mAh [package=lipo-1000]
  M2 = RioRand LM2596
  X1 = USB Connectors [package=usb-microb]  # not connected
  M3 = fc-51 [package=THT]
  M4 = fc-51 [package=THT]
  A3 = Sparkfun sen18642  # not connected
  Part3 = InvenSense MPU6050  # not connected
  A4 = Hi-link HLK-LD2410C  # not connected
  A5 = Jetson Nano  # not connected
  U2 = LIPO-2000mAh [package=lipo-2000]  # not connected
  Part6 = I2C level shifter bidirectional

nets:
  N1: HC-SR04_Sensor_1.VCC, M3.pin3, Part6.HV
  N2: HC-SR04_Sensor_1.TRIG, Part6.HV1
  N3: HC-SR04_Sensor_1.ECHO, Part6.HV2
  GND: HC-SR04_Sensor_1.GND, M3.pin2, Part6.GND
  N4: U1.+, M2.Pin_1
  N5: U1.-, M2.Pin_2
  N6: M3.pin1, Part6.HV3
  N7: M4.pin1, Part6.HV4

notes:
  REd=5V/6V power, Pink = Signal, Black = ground, Orange = 3.3V power
  SR04 is 5V. Fish sensor is 5V
  motors - encoder can be 3.3-5V. Output will be according to input
  Vl53L5CX is 3.3V power and
  https://learn.sparkfun.com/tutorials/qwiic-tof-imager---vl53l5cx-hookup-guide
  LD2450 power is 5V,200mA. It's Serial port (UART?) TxRx is 3.3V, default baud 256k
  MPU6050 is 3.3 or 5V as per power supply
  ESP32-Pico pins GP39 and GND are interchanged in this model. But onreal piece they are as per datasheet

custom parts:
  RPlidar A2M8: .The RPLIDAR A2 is the next generation low cost 360 degree 2D laser scanner (LIDAR) solution developed by SLAMTEC. It can take up to 4000 samples of laser ranging per second with high rotation speed. And equipped with SLAMTEC patented OPTMAG technology, it breakouts the life limitation of traditional LIDAR system so as to work stably for a long time.
  Sparkfun sen18642: The SparkFun Qwiic ToF Imager is built around VL53L5CX from ST Electronics; a state of the art, Time-of-Flight (ToF), multizone ranging sensor.
  Hi-link HLK-LD2410C: LD2410C is a high-sensitivity 24GHz human presence status sensing module. bb reversed for on perfboard in breadboard.
